// Logisim project alu.circ as structural Verilog: 1 circuit, main circuit alu
module alu (
  input  [31:0] A,
  input  [31:0] B,
  input  [3:0] ALUSel,
  output [31:0] ALUResult
);

  wire [0:0] O2;
  wire [31:0] add0, O0, O1, O4, O5, O6, O7, O8, O9, O11, O12, O13;

  Adder #(.width(32)) adder_1 (.a(A), .b(B), .out(O0));  // open: cin, cout
  Shifter #(.width(32)) shifter_1 (.in(A), .\dist (B[4:0]), .out(O1));
  Subtractor #(.width(32)) subtractor_1 (.a(A), .b(B), .out(O12));  // open: bin, bout
  assign O7 = A & B;  // AND_Gate and_1, 32 bits wide
  Comparator #(.width(32)) comparator_1 (.a(A), .b(B), .lt(O2[0]));  // open: gt, eq
  assign O4 = A ^ B;  // XOR_Gate xor_1, 32 bits wide
  Multiplier #(.mode("twosComplement"), .width(32)) multiplier_1 (.a(A), .b(B), .out(O8), .cout(O9));  // open: cin
  Shifter #(.shift("ar"), .width(32)) shifter_2 (.in(A), .\dist (B[4:0]), .out(O13));
  Adder #(.width(32)) adder_2 (.a(A), .b(B), .out(add0));  // open: cin, cout
  Shifter #(.shift("lr"), .width(32)) shifter_3 (.in(A), .\dist (B[4:0]), .out(O5));
  assign O6 = A | B;  // OR_Gate or_1, 32 bits wide
  Multiplier #(.width(32)) multiplier_2 (.a(A), .b(B), .cout(O11));  // open: out, cin
  Multiplexer #(.select(4), .width(32)) multiplexer_1 (
    .in0(O0), .in1(O1), .in2({{31{1'b0}}, O2[0]}), .in4(O4), .in5(O5), .in6(O6), .in7(O7), .in8(O8),
    .in9(O9), .in11(O11), .in12(O12), .in13(O13), .in15(B), .out(ALUResult), .sel(ALUSel));  // open: in3, in10, in14

  // Notes on the sheet:
  //   INPUTS to your circuit
  //   DON'T CHANGE THE LOCATIONS OF THE INPUTS AND OUTPUTS!
  //   OUTPUT from your circuit
endmodule
