// Logisim project control-logic.circ as structural Verilog: 1 circuit, main circuit control_logic
module control_logic (
  input  [31:0] Instruction,
  input  BrEq,
  input  BrLt,
  output PCSel,
  output RegWEn,
  output [2:0] ImmSel,
  output BrUn,
  output ASel,
  output BSel,
  output [3:0] ALUSel,
  output MemWEn,
  output [1:0] WBSel
);

  wire and_33_out, and_34_out, and_35_out, and_36_out, comparator_15_eq, comparator_16_eq, comparator_17_eq,
       comparator_18_eq, comparator_19_eq, comparator_20_eq, comparator_21_eq, comparator_22_eq,
       comparator_23_eq, comparator_24_eq, comparator_25_eq, comparator_26_eq, comparator_27_eq,
       comparator_28_eq, comparator_29_eq, comparator_30_eq, comparator_31_eq, comparator_32_eq,
       comparator_33_eq, comparator_34_eq, comparator_35_eq, comparator_36_eq, comparator_37_eq,
       comparator_38_eq, comparator_39_eq, comparator_40_eq, comparator_41_eq, comparator_42_eq,
       comparator_43_eq, comparator_44_eq, comparator_45_eq, comparator_46_eq, IS_ADD, IS_ADD_MUL_SUB,
       IS_ADDI, IS_AND, IS_ANDI, IS_ARITH, IS_AUIPC, IS_B, IS_BEQ, IS_BGE, IS_BGEU, IS_BLT, IS_BLTU, IS_BNE,
       IS_I, IS_JAL, IS_JALR, IS_L, IS_LB, IS_LH, IS_LOGICAL, IS_LUI, IS_LW, IS_MUL, IS_MULH, IS_MULHU,
       IS_OR, IS_ORI, IS_R, IS_S, IS_SB, IS_SH, IS_SLL, IS_SLL_MULH, IS_SLLI, IS_SLT, IS_SLTI, IS_SRA,
       IS_SRA_SRL, IS_SRAI, IS_SRL, IS_SRLI, IS_SUB, IS_SW, IS_XOR, IS_XORI, not_1_out, not_2_out, or_1_out,
       or_2_out, or_3_out;
  wire [5:0] ROM_INPUT;
  wire [15:14] rom_1_data;

  Comparator #(.width(7)) comparator_1 (.a(Instruction[6:0]), .b(7'b0010011), .eq(IS_I));  // open: gt, lt
  Comparator #(.width(7)) comparator_2 (.a(Instruction[6:0]), .b(7'b0110011), .eq(IS_R));  // open: gt, lt
  Comparator #(.width(7)) comparator_3 (.a(Instruction[6:0]), .b(7'b1100011), .eq(IS_B));  // open: gt, lt
  Comparator #(.width(7)) comparator_4 (.a(Instruction[6:0]), .b(7'b0000011), .eq(IS_L));  // open: gt, lt
  Comparator #(.width(7)) comparator_5 (.a(Instruction[6:0]), .b(7'b0100011), .eq(IS_S));  // open: gt, lt
  Comparator #(.width(7)) comparator_6 (.a(Instruction[31:25]), .b({7{1'b0}}), .eq(IS_LOGICAL));  // open: gt, lt
  Comparator #(.width(7)) comparator_7 (.a(Instruction[31:25]), .b(7'b0100000), .eq(IS_ARITH));  // open: gt, lt
  Comparator #(.width(3)) comparator_8 (.a(Instruction[14:12]), .b(3'b000), .eq(IS_ADD_MUL_SUB));  // open: gt, lt
  Comparator #(.width(3)) comparator_9 (.a(Instruction[14:12]), .b(3'b001), .eq(IS_SLL_MULH));  // open: gt, lt
  Comparator #(.width(3)) comparator_10 (.a(Instruction[14:12]), .b(3'b101), .eq(IS_SRA_SRL));  // open: gt, lt
  Comparator #(.width(7)) comparator_11 (.a(Instruction[6:0]), .b(7'b0010111), .eq(IS_AUIPC));  // open: gt, lt
  Comparator #(.width(7)) comparator_12 (.a(Instruction[6:0]), .b(7'b0110111), .eq(IS_LUI));  // open: gt, lt
  Comparator #(.width(7)) comparator_13 (.a(Instruction[6:0]), .b(7'b1101111), .eq(IS_JAL));  // open: gt, lt
  Comparator #(.width(7)) comparator_14 (.a(Instruction[6:0]), .b(7'b1100111), .eq(IS_JALR));  // open: gt, lt
  ROM #(.addrWidth(6), .dataWidth(16)) rom_1 (
    .addr(ROM_INPUT), .data({rom_1_data, WBSel, MemWEn, ALUSel, BSel, ASel, BrUn, ImmSel, RegWEn}));
  Comparator #(.width(7)) comparator_15 (.a(Instruction[31:25]), .b({7{1'b0}}), .eq(comparator_15_eq));  // open: gt, lt
  Comparator #(.width(7)) comparator_16 (
    .a(Instruction[31:25]), .b(7'b0000001), .eq(comparator_16_eq));  // open: gt, lt
  Comparator #(.width(7)) comparator_17 (
    .a(Instruction[31:25]), .b(7'b0100000), .eq(comparator_17_eq));  // open: gt, lt
  Comparator #(.width(7)) comparator_18 (.a(Instruction[31:25]), .b({7{1'b0}}), .eq(comparator_18_eq));  // open: gt, lt
  Comparator #(.width(7)) comparator_19 (
    .a(Instruction[31:25]), .b(7'b0000001), .eq(comparator_19_eq));  // open: gt, lt
  Comparator #(.width(7)) comparator_20 (.a(Instruction[31:25]), .b({7{1'b0}}), .eq(comparator_20_eq));  // open: gt, lt
  Comparator #(.width(7)) comparator_21 (
    .a(Instruction[31:25]), .b(7'b0100000), .eq(comparator_21_eq));  // open: gt, lt
  Comparator #(.width(3)) comparator_22 (.a(Instruction[14:12]), .b(3'b000), .eq(comparator_22_eq));  // open: gt, lt
  Comparator #(.width(3)) comparator_23 (.a(Instruction[14:12]), .b(3'b001), .eq(comparator_23_eq));  // open: gt, lt
  Comparator #(.width(3)) comparator_24 (.a(Instruction[14:12]), .b(3'b010), .eq(comparator_24_eq));  // open: gt, lt
  Comparator #(.width(3)) comparator_25 (.a(Instruction[14:12]), .b(3'b100), .eq(comparator_25_eq));  // open: gt, lt
  Comparator #(.width(3)) comparator_26 (.a(Instruction[14:12]), .b(3'b110), .eq(comparator_26_eq));  // open: gt, lt
  Comparator #(.width(3)) comparator_27 (.a(Instruction[14:12]), .b(3'b111), .eq(comparator_27_eq));  // open: gt, lt
  Comparator #(.width(3)) comparator_28 (.a(Instruction[14:12]), .b(3'b101), .eq(comparator_28_eq));  // open: gt, lt
  Comparator #(.width(3)) comparator_29 (.a(Instruction[14:12]), .b(3'b101), .eq(comparator_29_eq));  // open: gt, lt
  and and_1 (IS_SRAI, comparator_29_eq, IS_ARITH, IS_I);
  and and_2 (IS_ADD, IS_ADD_MUL_SUB, comparator_15_eq, IS_R);
  and and_3 (IS_MUL, IS_ADD_MUL_SUB, comparator_16_eq, IS_R);
  and and_4 (IS_SUB, IS_ADD_MUL_SUB, comparator_17_eq, IS_R);
  and and_5 (IS_SLL, IS_SLL_MULH, comparator_18_eq, IS_R);
  and and_6 (IS_MULH, IS_SLL_MULH, comparator_19_eq, IS_R);
  Comparator #(.width(3)) comparator_30 (.a(Instruction[14:12]), .b(3'b011), .eq(comparator_30_eq));  // open: gt, lt
  and and_7 (IS_MULHU, comparator_30_eq, IS_R);
  Comparator #(.width(3)) comparator_31 (.a(Instruction[14:12]), .b(3'b010), .eq(comparator_31_eq));  // open: gt, lt
  and and_8 (IS_SLT, comparator_31_eq, IS_R);
  Comparator #(.width(3)) comparator_32 (.a(Instruction[14:12]), .b(3'b100), .eq(comparator_32_eq));  // open: gt, lt
  and and_9 (IS_XOR, comparator_32_eq, IS_R);
  Comparator #(.width(3)) comparator_33 (.a(Instruction[14:12]), .b(3'b110), .eq(comparator_33_eq));  // open: gt, lt
  Comparator #(.width(3)) comparator_34 (.a(Instruction[14:12]), .b(3'b111), .eq(comparator_34_eq));  // open: gt, lt
  Comparator #(.width(3)) comparator_35 (.a(Instruction[14:12]), .b(3'b000), .eq(comparator_35_eq));  // open: gt, lt
  Comparator #(.width(3)) comparator_36 (.a(Instruction[14:12]), .b(3'b001), .eq(comparator_36_eq));  // open: gt, lt
  Comparator #(.width(3)) comparator_37 (.a(Instruction[14:12]), .b(3'b100), .eq(comparator_37_eq));  // open: gt, lt
  Comparator #(.width(3)) comparator_38 (.a(Instruction[14:12]), .b(3'b101), .eq(comparator_38_eq));  // open: gt, lt
  Comparator #(.width(3)) comparator_39 (.a(Instruction[14:12]), .b(3'b110), .eq(comparator_39_eq));  // open: gt, lt
  Comparator #(.width(3)) comparator_40 (.a(Instruction[14:12]), .b(3'b111), .eq(comparator_40_eq));  // open: gt, lt
  Comparator #(.width(3)) comparator_41 (.a(Instruction[14:12]), .b(3'b000), .eq(comparator_41_eq));  // open: gt, lt
  Comparator #(.width(3)) comparator_42 (.a(Instruction[14:12]), .b(3'b001), .eq(comparator_42_eq));  // open: gt, lt
  Comparator #(.width(3)) comparator_43 (.a(Instruction[14:12]), .b(3'b010), .eq(comparator_43_eq));  // open: gt, lt
  Comparator #(.width(3)) comparator_44 (.a(Instruction[14:12]), .b(3'b000), .eq(comparator_44_eq));  // open: gt, lt
  Comparator #(.width(3)) comparator_45 (.a(Instruction[14:12]), .b(3'b001), .eq(comparator_45_eq));  // open: gt, lt
  Comparator #(.width(3)) comparator_46 (.a(Instruction[14:12]), .b(3'b010), .eq(comparator_46_eq));  // open: gt, lt
  and and_10 (IS_ADDI, comparator_22_eq, IS_I);
  and and_11 (IS_SLLI, comparator_23_eq, IS_I);
  and and_12 (IS_SLTI, comparator_24_eq, IS_I);
  and and_13 (IS_XORI, comparator_25_eq, IS_I);
  and and_14 (IS_ORI, comparator_26_eq, IS_I);
  and and_15 (IS_ANDI, comparator_27_eq, IS_I);
  and and_16 (IS_SRLI, comparator_28_eq, IS_LOGICAL, IS_I);
  and and_17 (IS_SRL, IS_SRA_SRL, comparator_20_eq, IS_R);
  and and_18 (IS_SRA, IS_SRA_SRL, comparator_21_eq, IS_R);
  and and_19 (IS_OR, comparator_33_eq, IS_R);
  and and_20 (IS_AND, comparator_34_eq, IS_R);
  and and_21 (IS_BEQ, comparator_35_eq, IS_B);
  and and_22 (IS_BNE, comparator_36_eq, IS_B);
  and and_23 (IS_BLT, comparator_37_eq, IS_B);
  and and_24 (IS_BGE, comparator_38_eq, IS_B);
  and and_25 (IS_BLTU, comparator_39_eq, IS_B);
  and and_26 (IS_BGEU, comparator_40_eq, IS_B);
  and and_27 (IS_LB, comparator_41_eq, IS_L);
  and and_28 (IS_LH, comparator_42_eq, IS_L);
  and and_29 (IS_LW, comparator_43_eq, IS_L);
  and and_30 (IS_SB, comparator_44_eq, IS_S);
  and and_31 (IS_SH, comparator_45_eq, IS_S);
  and and_32 (IS_SW, comparator_46_eq, IS_S);
  or or_1 (or_1_out, IS_JAL, IS_JALR);
  not not_1 (not_1_out, BrEq);
  or or_2 (or_2_out, IS_BLT, IS_BLTU);
  or or_3 (or_3_out, IS_BGE, IS_BGEU);
  not not_2 (not_2_out, BrLt);
  and and_33 (and_33_out, IS_BEQ, BrEq);
  and and_34 (and_34_out, IS_BNE, not_1_out);
  and and_35 (and_35_out, or_2_out, BrLt);
  and and_36 (and_36_out, or_3_out, not_2_out);
  or or_4 (PCSel, and_33_out, and_34_out, or_1_out, and_35_out, and_36_out);
  Priority_Encoder #(.select_enc(6)) priority_encoder_1 (
    .in0(IS_ADD), .in1(IS_MUL), .in2(IS_SUB), .in3(IS_SLL), .in4(IS_MULH), .in5(IS_MULHU), .in6(IS_SLT),
    .in7(IS_XOR), .in8(IS_SRL), .in9(IS_SRA), .in10(IS_OR), .in11(IS_AND), .in12(IS_LB), .in13(IS_LH),
    .in14(IS_LW), .in15(IS_ADDI), .in16(IS_SLLI), .in17(IS_SLTI), .in18(IS_XORI), .in19(IS_SRLI),
    .in20(IS_SRAI), .in21(IS_ORI), .in22(IS_ANDI), .in23(IS_SB), .in24(IS_SH), .in25(IS_SW), .in26(IS_BEQ),
    .in27(IS_BNE), .in28(IS_BLT), .in29(IS_BGE), .in30(IS_BLTU), .in31(IS_BGEU), .in32(IS_AUIPC),
    .in33(IS_LUI), .in34(IS_JAL), .in35(IS_JALR), .out(ROM_INPUT));  // open: in36, in37, in38, in39, in40, in41, in42, in43, in44, in45, in46, in47, in48, in49, in50, in51, in52, in53, in54, in55, in56, in57, in58, in59, in60, in61, in62, in63, gs, en_out, en_in

  // Other names for the same wires on the sheet: OPCODE[6:0] = Instruction[6:0]; FUNC3[2:0] = Instruction[14:12];
  //   FUNC7[6:0] = Instruction[31:25]

  // Notes on the sheet:
  //   INPUTS to your circuit
  //   contents of rom_1 (hex, n*v repeats v):
  //   100f 140f 160f 108f 148f 158f 110f 120f 128f 168f 130f 138f 41 41 41 1041 10c1 1141 1241 12c1 16c1
  //   1341 13c1 842 842 842 4*64 74 74 1067 17e7 2069 2041
  //   ROM FOR CONTROL LOGIC
  //   DON'T CHANGE THE LOCATIONS OF THE INPUTS AND OUTPUTS!
  //   This is only if you choose to do the ROM option
  //   OUTPUT from your circuit
endmodule
