// Logisim project cpu.circ as structural Verilog: 1 circuit, main circuit cpu
module cpu (
  input  clk,
  input  [31:0] Instruction,
  input  [31:0] MemReadData,
  output [31:0] MemAddress,
  output [31:0] ProgramCounter,
  output [31:0] ra,
  output [31:0] sp,
  output [31:0] t0,
  output [31:0] t1,
  output [31:0] t2,
  output [31:0] s0,
  output [31:0] s1,
  output [31:0] a0,
  output [3:0] MemWriteMask,
  output [31:0] MemWriteData
);

  wire ASEL, BREQ, BRLT, BRUN, BSEL, MEMWEN, PCSEL, REGWEN;
  wire [1:0] WBSEL;
  wire [2:0] IMMSEL;
  wire [3:0] ALUSEL;
  wire [31:0] IMM, Instruction1, MEMout, multiplexer_1_out, multiplexer_2_out, multiplexer_3_out,
       multiplexer_4_out, multiplexer_5_out, PC4, ProgramCounter1, READ1, READ2;

  Adder #(.width(32)) adder_1 (.a(ProgramCounter), .b(32'h4), .out(PC4));  // open: cin, cout
  Register #(.width(32)) PC (.D(multiplexer_1_out), .clk(clk), .Q(ProgramCounter));  // open: en, clr
  Multiplexer #(.width(32)) multiplexer_1 (.in0(PC4), .in1(MemAddress), .out(multiplexer_1_out), .sel(PCSEL));
  Multiplexer #(.width(32)) multiplexer_2 (.in0(Instruction), .in1(32'h13), .out(multiplexer_2_out), .sel(PCSEL));
  Register #(.width(32)) register_1 (.D(multiplexer_2_out), .clk(clk), .Q(Instruction1));  // open: en, clr
  Multiplexer #(.select(2), .width(32)) multiplexer_3 (
    .in0(MEMout), .in1(MemAddress), .in2(ProgramCounter), .out(multiplexer_3_out), .sel(WBSEL));  // open: in3
  control_logic control_logic_1 (
    .PCSel(PCSEL), .RegWEn(REGWEN), .ImmSel(IMMSEL), .BrUn(BRUN), .ASel(ASEL), .BSel(BSEL), .ALUSel(ALUSEL),
    .MemWEn(MEMWEN), .WBSel(WBSEL), .Instruction(Instruction1), .BrEq(BREQ), .BrLt(BRLT));
  regfile regfile_1 (
    .ReadIndex1(Instruction1[19:15]), .ReadIndex2(Instruction1[24:20]), .WriteIndex(Instruction1[11:7]),
    .WriteData(multiplexer_3_out), .RegWEn(REGWEN), .clk(clk), .ra(ra), .sp(sp), .t0(t0), .t1(t1), .t2(t2),
    .s0(s0), .s1(s1), .a0(a0), .ReadData1(READ1), .ReadData2(READ2));
  imm_gen imm_gen_1 (.Instruction(Instruction1), .ImmSel(IMMSEL), .Immediate(IMM));
  Multiplexer #(.width(32)) multiplexer_4 (.in0(READ1), .in1(ProgramCounter1), .out(multiplexer_4_out), .sel(ASEL));
  Multiplexer #(.width(32)) multiplexer_5 (.in0(READ2), .in1(IMM), .out(multiplexer_5_out), .sel(BSEL));
  alu alu_1 (.ALUResult(MemAddress), .A(multiplexer_4_out), .B(multiplexer_5_out), .ALUSel(ALUSEL));
  branch_comp branch_comp_1 (.BrData1(READ1), .BrData2(READ2), .BrUn(BRUN), .BrEq(BREQ), .BrLt(BRLT));
  Register #(.width(32)) register_2 (.D(ProgramCounter), .clk(clk), .Q(ProgramCounter1));  // open: en, clr
  partial_store partial_store_1 (
    .Instruction(Instruction1), .MemAddress(MemAddress), .DataFromReg(READ2), .MemWEn(MEMWEN),
    .MemWriteMask(MemWriteMask), .DataToMem(MemWriteData));
  partial_load partial_load_1 (
    .Instruction(Instruction1), .MemAddress(MemAddress), .DataFromMem(MemReadData), .DataToReg(MEMout));

  // Other names for the same wires on the sheet: ALUout[31:0] = MemAddress; RD[4:0] = Instruction1[11:7];
  //   RS1[4:0] = Instruction1[19:15]; RS2[4:0] = Instruction1[24:20]

  // Notes on the sheet:
  //   To IMEM
  //   IMEM (do **NOT** move this)
  //   From IMEM
  //   Inputs/Outputs for testing. Do **NOT** move these.
  //   It is OK to move the PC, RegFile, ALU, MEM, Branch Comp, Imm Gen, Partial Load, Partial Store and Control Logic to wherever is most convenient for you when constructing your CPU, and to delete this text
  //   To DMEM
  //   DMEM (do **NOT** move this)
  //   From DMEM
endmodule
