// Logisim project imm-gen.circ as structural Verilog: 1 circuit, main circuit imm_gen
module imm_gen (
  input  [31:0] Instruction,
  input  [2:0] ImmSel,
  output [31:0] Immediate
);

  wire [31:0] ImmediateI, ImmediateU;

  Shifter #(.shift("ar"), .width(32)) shifter_1 (.in(Instruction), .\dist (5'b10100), .out(ImmediateI));
  assign ImmediateU = 32'hfffff000 & Instruction;  // AND_Gate and_1, 32 bits wide
  Multiplexer #(.select(3), .width(32)) multiplexer_1 (
    .in0(ImmediateI), .in1({{21{Instruction[31]}}, Instruction[30:25], Instruction[11:7]}),
    .in2({{20{Instruction[31]}}, Instruction[7], Instruction[30:25], Instruction[11:8], 1'b0}),
    .in3(ImmediateU),
    .in4({{12{Instruction[31]}}, Instruction[19:12], Instruction[20], Instruction[30:21], 1'b0}),
    .out(Immediate), .sel(ImmSel));  // open: in5, in6, in7

  // Other names for the same wires on the sheet: ImmediateJ[31:1] = {{12{Instruction[31]}}, Instruction[19:12], Instruction[20], Instruction[30:21]};
  //   ImmediateB[31:1] = {{20{Instruction[31]}}, Instruction[7], Instruction[30:25], Instruction[11:8]};
  //   ImmediateS[31:0] = {{21{Instruction[31]}}, Instruction[30:25], Instruction[11:7]}

  // Notes on the sheet:
  //   INPUTS to your circuit
  //   DON'T CHANGE THE LOCATIONS OF THE INPUTS AND OUTPUTS!
  //   OUTPUT from your circuit
endmodule
