// Logisim project partial-load.circ as structural Verilog: 3 circuits, main circuit partial_load
module partial_load (
  input  [31:0] Instruction,
  input  [31:0] MemAddress,
  input  [31:0] DataFromMem,
  output [31:0] DataToReg
);

  wire IS_LB, IS_LH, IS_LW;
  wire [31:0] B0, B1, B2, B3, BOUT, H0, H1, H2, HOUT;

  Comparator #(.width(3)) comparator_1 (.a(Instruction[14:12]), .b(3'b000), .eq(IS_LB));  // open: gt, lt
  Comparator #(.width(3)) comparator_2 (.a(Instruction[14:12]), .b(3'b001), .eq(IS_LH));  // open: gt, lt
  Comparator #(.width(3)) comparator_3 (.a(Instruction[14:12]), .b(3'b010), .eq(IS_LW));  // open: gt, lt
  SignExt16 signext16_1 (.in_1(DataFromMem[15:0]), .out_2(H0));
  SignExt16 signext16_2 (.in_1(DataFromMem[31:16]), .out_2(H2));
  SignExt8 signext8_1 (.in_1(DataFromMem[7:0]), .out_2(B0));
  SignExt8 signext8_2 (.in_1(DataFromMem[15:8]), .out_2(B1));
  SignExt8 signext8_3 (.in_1(DataFromMem[23:16]), .out_2(B2));
  SignExt8 signext8_4 (.in_1(DataFromMem[31:24]), .out_2(B3));
  SignExt16 signext16_3 (.in_1(DataFromMem[23:8]), .out_2(H1));
  Multiplexer #(.select(2), .width(32)) multiplexer_1 (
    .in0(H0), .in1(H1), .in2(H2), .out(HOUT), .sel(MemAddress[1:0]));  // open: in3
  Multiplexer #(.select(2), .width(32)) multiplexer_2 (
    .in0(B0), .in1(B1), .in2(B2), .in3(B3), .out(BOUT), .sel(MemAddress[1:0]));
  Multiplexer #(.select(3), .width(32)) multiplexer_3 (
    .in1(BOUT), .in2(HOUT), .in4(DataFromMem), .out(DataToReg), .sel({IS_LW, IS_LH, IS_LB}));  // open: in0, in3, in5, in6, in7

  // Other names for the same wires on the sheet: FUNC3[2:0] = Instruction[14:12]; INDEX[1:0] = MemAddress[1:0]

  // Notes on the sheet:
  //   INPUTS to your circuit
  //   DON'T CHANGE THE LOCATIONS OF THE INPUTS AND OUTPUTS!
  //   OUTPUT from your circuit
endmodule

module SignExt8 (
  input  [7:0] in_1,
  output [31:0] out_2
);


  assign out_2 = {{25{in_1[7]}}, in_1[6:0]};
endmodule

module SignExt16 (
  input  [15:0] in_1,
  output [31:0] out_2
);


  assign out_2 = {{17{in_1[15]}}, in_1[14:0]};
endmodule
