// Logisim project partial-store.circ as structural Verilog: 1 circuit, main circuit partial_store
module partial_store (
  input  [31:0] Instruction,
  input  [31:0] MemAddress,
  input  [31:0] DataFromReg,
  input  MemWEn,
  output [3:0] MemWriteMask,
  output [31:0] DataToMem
);

  wire IS_SB, IS_SH, IS_SW;
  wire [3:0] BOUTMASK, HOUTMASK, multiplexer_6_out;
  wire [31:0] BOUT, HOUT;

  Comparator #(.width(3)) comparator_1 (.a(Instruction[14:12]), .b(3'b000), .eq(IS_SB));  // open: gt, lt
  Comparator #(.width(3)) comparator_2 (.a(Instruction[14:12]), .b(3'b001), .eq(IS_SH));  // open: gt, lt
  Comparator #(.width(3)) comparator_3 (.a(Instruction[14:12]), .b(3'b010), .eq(IS_SW));  // open: gt, lt
  Multiplexer #(.select(2), .width(32)) multiplexer_1 (
    .in0({{24{1'b0}}, DataFromReg[7:0]}), .in1({{16{1'b0}}, DataFromReg[7:0], {8{1'b0}}}),
    .in2({{8{1'b0}}, DataFromReg[7:0], {16{1'b0}}}), .in3({DataFromReg[7:0], {24{1'b0}}}), .out(BOUT),
    .sel(MemAddress[1:0]));
  Multiplexer #(.select(2), .width(32)) multiplexer_2 (
    .in0({{16{1'b0}}, DataFromReg[15:0]}), .in2({DataFromReg[15:0], {16{1'b0}}}), .out(HOUT),
    .sel(MemAddress[1:0]));  // open: in1, in3
  Multiplexer #(.select(2), .width(4)) multiplexer_3 (
    .in0(4'b0001), .in1(4'b0010), .in2(4'b0100), .in3(4'b1000), .out(BOUTMASK), .sel(MemAddress[1:0]));
  Multiplexer #(.select(3), .width(32)) multiplexer_4 (
    .in1(BOUT), .in2(HOUT), .in4(DataFromReg), .out(DataToMem), .sel({IS_SW, IS_SH, IS_SB}));  // open: in0, in3, in5, in6, in7
  Multiplexer #(.select(2), .width(4)) multiplexer_5 (
    .in0(4'b0011), .in2(4'b1100), .out(HOUTMASK), .sel(MemAddress[1:0]));  // open: in1, in3
  Multiplexer #(.select(3), .width(4)) multiplexer_6 (
    .in1(BOUTMASK), .in2(HOUTMASK), .in4(4'b1111), .out(multiplexer_6_out), .sel({IS_SW, IS_SH, IS_SB}));  // open: in0, in3, in5, in6, in7
  Multiplexer #(.width(4)) multiplexer_7 (.in0(4'b0000), .in1(multiplexer_6_out), .out(MemWriteMask), .sel(MemWEn));

  // Other names for the same wires on the sheet: FUNC3[2:0] = Instruction[14:12]; B0[7:0] = DataFromReg[7:0];
  //   B1[15:8] = DataFromReg[7:0]; B2[23:16] = DataFromReg[7:0]; B3[31:24] = DataFromReg[7:0];
  //   BPart[7:0] = DataFromReg[7:0]; H0[15:0] = DataFromReg[15:0]; H1[31:16] = DataFromReg[15:0];
  //   HPart[15:0] = DataFromReg[15:0]; INDEX[1:0] = MemAddress[1:0]

  // Notes on the sheet:
  //   INPUTS to your circuit
  //   DON'T CHANGE THE LOCATIONS OF THE INPUTS AND OUTPUTS!
  //   OUTPUT from your circuit
endmodule
