// Logisim project regfile.circ as structural Verilog: 1 circuit, main circuit regfile
module regfile (
  input  [4:0] ReadIndex1,
  input  [4:0] ReadIndex2,
  input  [4:0] WriteIndex,
  input  [31:0] WriteData,
  input  RegWEn,
  input  clk,
  output [31:0] ra,
  output [31:0] sp,
  output [31:0] t0,
  output [31:0] t1,
  output [31:0] t2,
  output [31:0] s0,
  output [31:0] s1,
  output [31:0] a0,
  output [31:0] ReadData1,
  output [31:0] ReadData2
);

  wire and_1_out, and_2_out, and_3_out, and_4_out, and_5_out, and_6_out, and_7_out, and_8_out, and_9_out,
       and_10_out, and_11_out, and_12_out, and_13_out, and_14_out, and_15_out, and_16_out, and_17_out,
       and_18_out, and_19_out, and_20_out, and_21_out, and_22_out, and_23_out, and_24_out, and_25_out,
       and_26_out, and_27_out, and_28_out, and_29_out, and_30_out, and_31_out, and_32_out, W0, W1, W2, W3,
       W4, W5, W6, W7, W8, W9, W10, W11, W12, W13, W14, W15, W16, W17, W18, W19, W20, W21, W22, W23, W24,
       W25, W26, W27, W28, W29, W30, W31;
  wire [31:0] R0, R3, R4, R11, R12, R13, R14, R15, R16, R17, R18, R19, R20, R21, R22, R23, R24, R25, R26,
       R27, R28, R29, R30, R31;

  Register #(.width(32)) register_1 (.D({32{1'b0}}), .en(and_1_out), .clk(clk), .Q(R0));  // open: clr
  and and_1 (and_1_out, W0, RegWEn);
  Register #(.width(32)) register_2 (.D(WriteData), .en(and_2_out), .clk(clk), .Q(R4));  // open: clr
  and and_2 (and_2_out, W4, RegWEn);
  Register #(.width(32)) register_3 (.D(WriteData), .en(and_3_out), .clk(clk), .Q(s0));  // open: clr
  and and_3 (and_3_out, W8, RegWEn);
  Register #(.width(32)) register_4 (.D(WriteData), .en(and_4_out), .clk(clk), .Q(R12));  // open: clr
  and and_4 (and_4_out, W12, RegWEn);
  Register #(.width(32)) register_5 (.D(WriteData), .en(and_5_out), .clk(clk), .Q(R16));  // open: clr
  and and_5 (and_5_out, W16, RegWEn);
  Register #(.width(32)) register_6 (.D(WriteData), .en(and_6_out), .clk(clk), .Q(R20));  // open: clr
  and and_6 (and_6_out, W20, RegWEn);
  Register #(.width(32)) register_7 (.D(WriteData), .en(and_7_out), .clk(clk), .Q(R24));  // open: clr
  and and_7 (and_7_out, W24, RegWEn);
  Register #(.width(32)) register_8 (.D(WriteData), .en(and_8_out), .clk(clk), .Q(R28));  // open: clr
  and and_8 (and_8_out, W28, RegWEn);
  Register #(.width(32)) register_9 (.D(WriteData), .en(and_9_out), .clk(clk), .Q(ra));  // open: clr
  and and_9 (and_9_out, W1, RegWEn);
  Register #(.width(32)) register_10 (.D(WriteData), .en(and_10_out), .clk(clk), .Q(t0));  // open: clr
  and and_10 (and_10_out, W5, RegWEn);
  Register #(.width(32)) register_11 (.D(WriteData), .en(and_11_out), .clk(clk), .Q(s1));  // open: clr
  and and_11 (and_11_out, W9, RegWEn);
  Register #(.width(32)) register_12 (.D(WriteData), .en(and_12_out), .clk(clk), .Q(R13));  // open: clr
  and and_12 (and_12_out, W13, RegWEn);
  Register #(.width(32)) register_13 (.D(WriteData), .en(and_13_out), .clk(clk), .Q(R17));  // open: clr
  and and_13 (and_13_out, W17, RegWEn);
  Register #(.width(32)) register_14 (.D(WriteData), .en(and_14_out), .clk(clk), .Q(R21));  // open: clr
  and and_14 (and_14_out, W21, RegWEn);
  Register #(.width(32)) register_15 (.D(WriteData), .en(and_15_out), .clk(clk), .Q(R25));  // open: clr
  and and_15 (and_15_out, W25, RegWEn);
  Register #(.width(32)) register_16 (.D(WriteData), .en(and_16_out), .clk(clk), .Q(R29));  // open: clr
  and and_16 (and_16_out, W29, RegWEn);
  Decoder #(.select(5)) decoder_1 (
    .out0(W0), .out1(W1), .out2(W2), .out3(W3), .out4(W4), .out5(W5), .out6(W6), .out7(W7), .out8(W8),
    .out9(W9), .out10(W10), .out11(W11), .out12(W12), .out13(W13), .out14(W14), .out15(W15), .out16(W16),
    .out17(W17), .out18(W18), .out19(W19), .out20(W20), .out21(W21), .out22(W22), .out23(W23), .out24(W24),
    .out25(W25), .out26(W26), .out27(W27), .out28(W28), .out29(W29), .out30(W30), .out31(W31),
    .sel(WriteIndex));  // open: en
  Register #(.width(32)) register_17 (.D(WriteData), .en(and_17_out), .clk(clk), .Q(sp));  // open: clr
  and and_17 (and_17_out, W2, RegWEn);
  Register #(.width(32)) register_18 (.D(WriteData), .en(and_18_out), .clk(clk), .Q(t1));  // open: clr
  and and_18 (and_18_out, W6, RegWEn);
  Register #(.width(32)) register_19 (.D(WriteData), .en(and_19_out), .clk(clk), .Q(a0));  // open: clr
  and and_19 (and_19_out, W10, RegWEn);
  Register #(.width(32)) register_20 (.D(WriteData), .en(and_20_out), .clk(clk), .Q(R14));  // open: clr
  and and_20 (and_20_out, W14, RegWEn);
  Register #(.width(32)) register_21 (.D(WriteData), .en(and_21_out), .clk(clk), .Q(R18));  // open: clr
  and and_21 (and_21_out, W18, RegWEn);
  Register #(.width(32)) register_22 (.D(WriteData), .en(and_22_out), .clk(clk), .Q(R22));  // open: clr
  and and_22 (and_22_out, W22, RegWEn);
  Register #(.width(32)) register_23 (.D(WriteData), .en(and_23_out), .clk(clk), .Q(R26));  // open: clr
  and and_23 (and_23_out, W26, RegWEn);
  Register #(.width(32)) register_24 (.D(WriteData), .en(and_24_out), .clk(clk), .Q(R30));  // open: clr
  and and_24 (and_24_out, W30, RegWEn);
  Register #(.width(32)) register_25 (.D(WriteData), .en(and_25_out), .clk(clk), .Q(R3));  // open: clr
  and and_25 (and_25_out, W3, RegWEn);
  Register #(.width(32)) register_26 (.D(WriteData), .en(and_26_out), .clk(clk), .Q(t2));  // open: clr
  and and_26 (and_26_out, W7, RegWEn);
  Register #(.width(32)) register_27 (.D(WriteData), .en(and_27_out), .clk(clk), .Q(R11));  // open: clr
  and and_27 (and_27_out, W11, RegWEn);
  Register #(.width(32)) register_28 (.D(WriteData), .en(and_28_out), .clk(clk), .Q(R15));  // open: clr
  and and_28 (and_28_out, W15, RegWEn);
  Register #(.width(32)) register_29 (.D(WriteData), .en(and_29_out), .clk(clk), .Q(R19));  // open: clr
  and and_29 (and_29_out, W19, RegWEn);
  Register #(.width(32)) register_30 (.D(WriteData), .en(and_30_out), .clk(clk), .Q(R23));  // open: clr
  and and_30 (and_30_out, W23, RegWEn);
  Register #(.width(32)) register_31 (.D(WriteData), .en(and_31_out), .clk(clk), .Q(R27));  // open: clr
  and and_31 (and_31_out, W27, RegWEn);
  Register #(.width(32)) register_32 (.D(WriteData), .en(and_32_out), .clk(clk), .Q(R31));  // open: clr
  and and_32 (and_32_out, W31, RegWEn);
  Multiplexer #(.select(5), .width(32)) multiplexer_1 (
    .in0(R0), .in1(ra), .in2(sp), .in3(R3), .in4(R4), .in5(t0), .in6(t1), .in7(t2), .in8(s0), .in9(s1),
    .in10(a0), .in11(R11), .in12(R12), .in13(R13), .in14(R14), .in15(R15), .in16(R16), .in17(R17),
    .in18(R18), .in19(R19), .in20(R20), .in21(R21), .in22(R22), .in23(R23), .in24(R24), .in25(R25),
    .in26(R26), .in27(R27), .in28(R28), .in29(R29), .in30(R30), .in31(R31), .out(ReadData1), .sel(ReadIndex1));
  Multiplexer #(.select(5), .width(32)) multiplexer_2 (
    .in0(R0), .in1(ra), .in2(sp), .in3(R3), .in4(R4), .in5(t0), .in6(t1), .in7(t2), .in8(s0), .in9(s1),
    .in10(a0), .in11(R11), .in12(R12), .in13(R13), .in14(R14), .in15(R15), .in16(R16), .in17(R17),
    .in18(R18), .in19(R19), .in20(R20), .in21(R21), .in22(R22), .in23(R23), .in24(R24), .in25(R25),
    .in26(R26), .in27(R27), .in28(R28), .in29(R29), .in30(R30), .in31(R31), .out(ReadData2), .sel(ReadIndex2));

  // Other names for the same wires on the sheet: R1[31:0] = ra; R2[31:0] = sp; R5[31:0] = t0; R6[31:0] = t1;
  //   R7[31:0] = t2; R8[31:0] = s0; R9[31:0] = s1; R10[31:0] = a0

  // Notes on the sheet:
  //   INPUTS to your circuit
  //   DON'T CHANGE THE LOCATIONS OF THE INPUTS AND OUTPUTS!
  //   These are DEBUG/TEST outputs from your circuit.
  //   OUTPUTS from your circuit
endmodule
